# Fritzing sketch UEC_SAC_Mod_A_Rev_1_3_1_borrador (saved by Fritzing 0.8.7b)
circuit board: 10cm x 10cm
circuit board: 5.5cm x 4.5cm
perfboards: 1

parts:
  330Ω = Resistor [tolerance=±5% resistance=4.7k package=THT]
  330Ω_2 = Resistor [tolerance=±5% resistance=1k package=THT]
  1N4001 = Rectifier Diode [part_number=1N4001 package="300 mil [THT]"]
  +_- = female pin header, 1 pin [form="♀ (female)"]
  V-AC_Out_1_A = female pin header, 1 pin [form="♀ (female)"]
  LED = LED - 3mm [color="Red (633nm)" package="3 mm [THT]"]
  V+ = female pin header, 1 pin [form="♀ (female)"]
  V- = female pin header, 1 pin [form="♀ (female)"]
  Artesanos_Industriales_del_Sur = female pin header, 1 pin [form="♀ (female)"]
  BY-SA_4 = female pin header, 1 pin [form="♀ (female)"]
  1N4001_2 = Rectifier Diode [part_number=1N4001 package="300 mil [THT]"]
  47uF = Electrolytic Capacitor [capacitance=47µF voltage=16V package="100 mil [THT, electrolytic]"]
  47uF_2 = Electrolytic Capacitor [capacitance=47µF voltage=16V package="100 mil [THT, electrolytic]"]
  0_1uF = Ceramic Capacitor [capacitance=100nF package="100 mil [THT, multilayer]"]
  UA+5V = Voltage Regulator - 5V [package="TO220 [THT]"]
  10kΩ = Resistor [tolerance=±5% resistance=10k package=THT]
  10kΩ_2 = Resistor [tolerance=±5% resistance=10k package=THT]
  100Ω = Resistor [tolerance=±5% resistance=100 package=THT]
  100Ω_2 = Resistor [tolerance=±5% resistance=100 package=THT]
  SW(+) = male pin header, 2 pins [form="♂ (male)"]
  SW(M) = male pin header, 2 pins [form="♂ (male)"]
  SW(-) = male pin header, 2 pins [form="♂ (male)"]
  150Ω = Resistor [tolerance=±5% resistance=150 package=THT]
  10kΩ_3 = Resistor [tolerance=±5% resistance=1k package=THT]
  47Ω_1/2W = Resistor [tolerance=±5% resistance=47 package=THT]
  FUSE_1 = female pin header, 1 pin [form="♀ (female)"]
  ------------------------ = female pin header, 1 pin [form="♀ (female)"]
  330Ω_3 = Resistor [tolerance=±5% resistance=4.7k package=THT]
  330Ω_4 = Resistor [tolerance=±5% resistance=1k package=THT]
  150Ω_2 = Resistor [tolerance=±5% resistance=150 package=THT]
  10kΩ_4 = Resistor [tolerance=±5% resistance=1k package=THT]
  1N4001_3 = Rectifier Diode [part_number=1N4001 package="300 mil [THT]"]
  FUSE_2 = female pin header, 1 pin [form="♀ (female)"]
  ------------------------_2 = female pin header, 1 pin [form="♀ (female)"]
  +_-_2 = female pin header, 1 pin [form="♀ (female)"]
  V-AC_Out_2 = female pin header, 1 pin [form="♀ (female)"]
  LED_2 = LED - 3mm [color="Red (633nm)" package="3 mm [THT]"]
  47Ω_1/2W_2 = Resistor [tolerance=±5% resistance=47 package=THT]
  330Ω_5 = Resistor [tolerance=±5% resistance=4.7k package=THT]
  330Ω_6 = Resistor [tolerance=±5% resistance=1k package=THT]
  150Ω_3 = Resistor [tolerance=±5% resistance=150 package=THT]
  10kΩ_5 = Resistor [tolerance=±5% resistance=1k package=THT]
  1N4001_4 = Rectifier Diode [part_number=1N4001 package="300 mil [THT]"]
  FUSE_3 = female pin header, 1 pin [form="♀ (female)"]
  ------------------------_3 = female pin header, 1 pin [form="♀ (female)"]
  +_-_3 = female pin header, 1 pin [form="♀ (female)"]
  V-AC_Out_3 = female pin header, 1 pin [form="♀ (female)"]
  LED_3 = LED - 3mm [color="Red (633nm)" package="3 mm [THT]"]
  100Ω_3 = Resistor [tolerance=±5% resistance=100 package=THT]
  100Ω_4 = Resistor [tolerance=±5% resistance=100 package=THT]
  10kΩ_6 = Resistor [tolerance=±5% resistance=10k package=THT]
  10kΩ_7 = Resistor [tolerance=±5% resistance=10k package=THT]
  100Ω_5 = Resistor [tolerance=±5% resistance=100 package=THT]
  V-IN = female pin header, 1 pin [form="♀ (female)"]
  V-OUT = female pin header, 1 pin [form="♀ (female)"]
  V-IN_2 = female pin header, 1 pin [form="♀ (female)"]
  V-OUT_2 = female pin header, 1 pin [form="♀ (female)"]
  V-IN_3 = female pin header, 1 pin [form="♀ (female)"]
  V-OUT_3 = female pin header, 1 pin [form="♀ (female)"]
  100nF/400V = female pin header, 1 pin [form="♀ (female)"]
  J15 = female pin header, 1 pin [form="♀ (female)"]
  J17 = female pin header, 1 pin [form="♀ (female)"]
  100nF/400V_2 = female pin header, 1 pin [form="♀ (female)"]
  J20 = female pin header, 1 pin [form="♀ (female)"]
  100nF/400V_3 = female pin header, 1 pin [form="♀ (female)"]
  47Ω_1/2W_3 = Resistor [tolerance=±5% resistance=47 package=THT]
  0_1uF_2 = Ceramic Capacitor [capacitance=100nF package="100 mil [THT, multilayer]"]
  100Ω_6 = Resistor [tolerance=±5% resistance=100 package=THT]
  ------------------------1 = female pin header, 2 pins [form="♀ (female)"]
  ------------------------2 = female pin header, 2 pins [form="♀ (female)"]
  ------------------------6 = female pin header, 2 pins [form="♀ (female)"]
  ------------------------5 = female pin header, 2 pins [form="♀ (female)"]
  ------------------------8 = female pin header, 2 pins [form="♀ (female)"]
  ------------------------7 = female pin header, 2 pins [form="♀ (female)"]
  ------------------------10 = female pin header, 2 pins [form="♀ (female)"]
  ------------------------9 = female pin header, 2 pins [form="♀ (female)"]
  10kΩ_8 = Resistor [tolerance=±5% resistance=10k package=THT]
  ------------------------22 = female pin header, 2 pins [form="♀ (female)"]
  ------------------------23 = female pin header, 2 pins [form="♀ (female)"]
  ------------------------24 = female pin header, 2 pins [form="♀ (female)"]
  V_In_100-240_AC = female pin header, 2 pins [form="♀ (female)"]
  Clock = male pin header, 4 pins [form="♂ (male)"]
  UA+3_3V = Voltage Regulator - 3.3V [package="TO220 [THT]"]
  LCD1 = male pin header, 3 pins [form="♂ (male)"]
  Soil_Moisture = female pin header, 2 pins [form="♀ (female)"]
  Field_Capacity = female pin header, 2 pins [form="♀ (female)"]
  +3_3V_GND = male pin header, 2 pins [form="♂ (male)"]
  +5V_GND = male pin header, 2 pins [form="♂ (male)"]
  N/C_GND = female pin header, 4 pins [form="♀ (female)"]
  LCD6 = male pin header, 4 pins [form="♂ (male)"]
  ------------------------26 = female pin header, 3 pins [form="♀ (female)"]
  10kΩ_9 = Resistor [tolerance=±5% resistance=10k package=THT]
  ------------------------17 = female pin header, 4 pins [form="♀ (female)"]
  SW(-)2 = male pin header, 2 pins [form="♂ (male)"]
  SW(-)1 = male pin header, 2 pins [form="♂ (male)"]
  A5_A4 = male pin header, 2 pins [form="♂ (male)"]
  ------------------------27 = female pin header, 2 pins [form="♀ (female)"]
  ------------------------28 = female pin header, 2 pins [form="♀ (female)"]
  ------------------------29 = female pin header, 2 pins [form="♀ (female)"]
  A7_A6 = male pin header, 2 pins [form="♂ (male)"]
  LCD2 = male pin header, 3 pins [form="♂ (male)"]
  LCD5 = male pin header, 3 pins [form="♂ (male)"]
  4k7Ω = Resistor [tolerance=±5% resistance=4.7k package=THT]
  2N2222A = NPN-Transistor [package="TO92 [THT]"]
  2N3904 = NPN-Transistor [package="TO92 [THT]"]
  2N3904_2 = NPN-Transistor [package="TO92 [THT]"]
  2N2222A_2 = NPN-Transistor [package="TO92 [THT]"]
  Arduino_Pro_Mini_5V = Arduino Pro Mini v13
  2N3904_3 = NPN-Transistor [package="TO92 [THT]"]
  Water_Level_Tank = female pin header, 3 pins [form="♀ (female)"]
  TX_N/C_RX = female pin header, 2 pins [form="♀ (female)"]
  RF_433MHz = rounded female pin header, 6 pins [form="♀ (female rounded)"]

nets:
  N1: 330Ω.Pin_0, 10kΩ_3.Pin_0, 2N3904.B
  N2: 330Ω.Pin_1, Arduino_Pro_Mini_5V.D2, RF_433MHz.pin3
  N3: 330Ω_2.Pin_0, 47uF_2.+, 0_1uF.1, UA+5V.output_voltage, SW(+).pin1, SW(M).pin1, SW(-).pin1, 150Ω.Pin_1, 330Ω_4.Pin_0, 150Ω_2.Pin_1, 330Ω_6.Pin_0, 150Ω_3.Pin_1, 10kΩ_8.Pin_0, Clock.pin3, UA+3_3V.input_voltage, LCD1.pin2, +5V_GND.pin1, N/C_GND.pin1, LCD6.pin3, ------------------------26.pin2, 10kΩ_9.Pin_0, ------------------------17.pin3, LCD2.pin2, LCD5.pin2, 4k7Ω.Pin_0, RF_433MHz.pin4
  N4: 330Ω_2.Pin_1, LED.cathode
  N5: 1N4001.cathode, V-AC_Out_1_A.pin1, 150Ω.Pin_0
  N6: 1N4001.anode, +_-.pin1, LED.anode, 2N3904.C
  N7: V+.pin1, 1N4001_2.cathode, SW(-)2.pin1
  N8: V-.pin1, 1N4001_2.anode, SW(-)1.pin1
  N9: Artesanos_Industriales_del_Sur.pin1, V-IN.pin1, V-IN_2.pin1, V-IN_3.pin1, J15.pin1, J17.pin1, J20.pin1, ------------------------9.pin1, ------------------------9.pin2, SW(-)1.pin2
  N10: BY-SA_4.pin1, ------------------------1.pin1, ------------------------1.pin2, ------------------------6.pin1, ------------------------6.pin2, ------------------------8.pin1, ------------------------8.pin2, ------------------------10.pin1, ------------------------10.pin2, SW(-)2.pin2, ------------------------27.pin1, ------------------------27.pin2
  GND: 47uF.-, 47uF_2.-, 0_1uF.0, UA+5V.GND, 10kΩ_2.Pin_1, 10kΩ_3.Pin_1, 10kΩ_4.Pin_1, 10kΩ_5.Pin_1, 10kΩ_6.Pin_1, 10kΩ_7.Pin_1, 0_1uF_2.0, Clock.pin4, UA+3_3V.GND, LCD1.pin1, +3_3V_GND.pin2, +5V_GND.pin2, N/C_GND.pin4, LCD6.pin4, ------------------------26.pin3, ------------------------17.pin4, LCD2.pin1, LCD5.pin1, 2N3904.E, 2N3904_2.E, Arduino_Pro_Mini_5V.GND, 2N3904_3.E, RF_433MHz.pin5
  N11: 47uF.+, UA+5V.input_voltage, 0_1uF_2.1, Arduino_Pro_Mini_5V.RAW
  N12: 10kΩ.Pin_0, Water_Level_Tank.pin3
  N13: 10kΩ.Pin_1, Water_Level_Tank.pin1
  N14: 10kΩ_2.Pin_0, SW(-).pin2, Arduino_Pro_Mini_5V.D7
  N15: 100Ω.Pin_1, Soil_Moisture.pin1
  N16: 100Ω_2.Pin_1, 2N2222A.E
  N17: SW(+).pin2, 10kΩ_7.Pin_0, Arduino_Pro_Mini_5V.D9_PWM
  N18: SW(M).pin2, 10kΩ_6.Pin_0, Arduino_Pro_Mini_5V.D8
  N19: 47Ω_1/2W.Pin_0, 100nF/400V_3.pin1
  N20: 47Ω_1/2W.Pin_1, FUSE_1.pin1, V-OUT_2.pin1
  N21: ------------------------.pin1, ------------------------2.pin1, ------------------------2.pin2, ------------------------28.pin1, ------------------------28.pin2
  N22: 330Ω_3.Pin_0, 10kΩ_4.Pin_0, 2N3904_2.B
  N23: 330Ω_3.Pin_1, Arduino_Pro_Mini_5V.D3_PWM, RF_433MHz.pin2
  N24: 330Ω_4.Pin_1, LED_2.cathode
  N25: 150Ω_2.Pin_0, 1N4001_3.cathode, V-AC_Out_2.pin1
  N26: 1N4001_3.anode, +_-_2.pin1, LED_2.anode, 2N3904_2.C
  N27: FUSE_2.pin1, 47Ω_1/2W_2.Pin_1, V-OUT.pin1
  N28: ------------------------_2.pin1, ------------------------5.pin1, ------------------------5.pin2
  N29: 47Ω_1/2W_2.Pin_0, 100nF/400V_2.pin1
  N30: 330Ω_5.Pin_0, 10kΩ_5.Pin_0, 2N3904_3.B
  N31: 330Ω_5.Pin_1, Arduino_Pro_Mini_5V.D4, RF_433MHz.pin1
  N32: 330Ω_6.Pin_1, LED_3.cathode
  N33: 150Ω_3.Pin_0, 1N4001_4.cathode, V-AC_Out_3.pin1
  N34: 1N4001_4.anode, +_-_3.pin1, LED_3.anode, 2N3904_3.C
  N35: FUSE_3.pin1, V-OUT_3.pin1, 47Ω_1/2W_3.Pin_1
  N36: ------------------------_3.pin1, ------------------------7.pin1, ------------------------7.pin2
  N37: 100Ω_3.Pin_1, Field_Capacity.pin1
  N38: 100Ω_4.Pin_1, 2N2222A_2.E
  N39: 100Ω_5.Pin_0, 2N2222A.C
  N40: 100nF/400V.pin1, 47Ω_1/2W_3.Pin_0
  N41: 100Ω_6.Pin_1, 2N2222A_2.C
  N42: 10kΩ_8.Pin_1, ------------------------17.pin1, Arduino_Pro_Mini_5V.A1
  N43: ------------------------22.pin1, ------------------------22.pin2, ------------------------23.pin1, ------------------------23.pin2, ------------------------24.pin1, ------------------------24.pin2, V_In_100-240_AC.pin1, V_In_100-240_AC.pin2, ------------------------29.pin1, ------------------------29.pin2
  N44: Clock.pin1, A5_A4.pin2
  N45: Clock.pin2, A5_A4.pin1
  N46: UA+3_3V.output_voltage, +3_3V_GND.pin1, N/C_GND.pin2
  N47: LCD1.pin3, Arduino_Pro_Mini_5V.D10_PWM/SS
  N48: Soil_Moisture.pin2, 2N2222A.B
  N49: Field_Capacity.pin2, 2N2222A_2.B
  N50: LCD6.pin1, Arduino_Pro_Mini_5V.D11_PWM/MOSI
  N51: LCD6.pin2, Arduino_Pro_Mini_5V.D12/MISO
  N52: ------------------------26.pin1, 10kΩ_9.Pin_1, Arduino_Pro_Mini_5V.D6_PWM
  N53: ------------------------17.pin2, Arduino_Pro_Mini_5V.A0
  N54: A7_A6.pin1, LCD2.pin3
  N55: LCD5.pin3, 4k7Ω.Pin_1, Arduino_Pro_Mini_5V.D13/SCK
  N56: Arduino_Pro_Mini_5V.D0/TX, TX_N/C_RX.pin2
  N57: Arduino_Pro_Mini_5V.D1/RX, TX_N/C_RX.pin1

notes:
  -  + Rx Tx
  UEC_AC_Mod. A-3S Rev.1.3
  T-H AIR  +   -
  SSR
  CAM +  -
  SCL SDA +  -
  L  N  G
  Artesanos Industriales del Sur  aisur.org
  Power Supply 100-240VAC->9-12VDC
  SM-2
  D1 +  -
  D3    +  -
  CO2
  +  -
  SM-1
  DS1307
  RXI<---
  TXO<---
  EXTENSION
  Micro-controller
  STª
  __________________________
  +3.3V
  +5V
  Data Logger
  A6
  ______
  LCD
  Wi-Fi/RF
  Extra Sensors
  FLOW  +    -
  _____
  If External Power Supply 9VDC
  +
  Out 1.B
  DAT
  sacultivo.com
  GND
