# Fritzing sketch UEC_SAC_Mod_A_Rev_1_2_1 (saved by Fritzing 0.8.3b)
circuit board: 10cm x 10cm
perfboards: 1

parts:
  LCD = male pin header, 4 pins [form="♂ (male)"]
  330Ω = Resistor [tolerance=±5% resistance=4.7k package=THT]
  330Ω_2 = Resistor [tolerance=±5% resistance=1k package=THT]
  1N4001 = Rectifier Diode [part_number=1N4001 package="300 mil [THT]"]
  +_- = female pin header, 1 pin [form="♀ (female)"]
  V-AC_Out_1 = female pin header, 1 pin [form="♀ (female)"]
  LED = LED - 3mm [color="Red (633nm)" package="3 mm [THT]"]
  V+ = female pin header, 1 pin [form="♀ (female)"]
  V- = female pin header, 1 pin [form="♀ (female)"]
  Artesanos_Industriales_del_Sur = female pin header, 1 pin [form="♀ (female)"]
  BY-SA_3_1 = female pin header, 1 pin [form="♀ (female)"]
  1N4001_2 = Rectifier Diode [part_number=1N4001 package="300 mil [THT]"]
  47uF = Electrolytic Capacitor [capacitance=47µF voltage=16V package="100 mil [THT, electrolytic]"]
  47uF_2 = Electrolytic Capacitor [capacitance=47µF voltage=16V package="100 mil [THT, electrolytic]"]
  0_1uF = Ceramic Capacitor [capacitance=100nF package="100 mil [THT, multilayer]"]
  UA+5V = Voltage Regulator - 5V [package="TO220 [THT]"]
  10kΩ = Resistor [tolerance=±5% resistance=10k package=THT]
  10kΩ_2 = Resistor [tolerance=±5% resistance=10k package=THT]
  2N2222A = NPN-Transistor [package="TO92 [THT]"]
  100Ω = Resistor [tolerance=±5% resistance=100 package=THT]
  100Ω_2 = Resistor [tolerance=±5% resistance=100 package=THT]
  SW_+ = male pin header, 2 pins [form="♂ (male)"]
  SW_M = male pin header, 2 pins [form="♂ (male)"]
  SW_- = male pin header, 2 pins [form="♂ (male)"]
  150Ω = Resistor [tolerance=±5% resistance=150 package=THT]
  10kΩ_3 = Resistor [tolerance=±5% resistance=1k package=THT]
  47Ω_1/2W = Resistor [tolerance=±5% resistance=47 package=THT]
  2N3904 = NPN-Transistor [part_number=BC547 package="TO92 [THT]"]
  FUSE_1 = female pin header, 1 pin [form="♀ (female)"]
  ------------------------ = female pin header, 1 pin [form="♀ (female)"]
  330Ω_3 = Resistor [tolerance=±5% resistance=4.7k package=THT]
  330Ω_4 = Resistor [tolerance=±5% resistance=1k package=THT]
  150Ω_2 = Resistor [tolerance=±5% resistance=150 package=THT]
  10kΩ_4 = Resistor [tolerance=±5% resistance=1k package=THT]
  2N3904_2 = NPN-Transistor [part_number=BC547 package="TO92 [THT]"]
  1N4001_3 = Rectifier Diode [part_number=1N4001 package="300 mil [THT]"]
  FUSE_2 = female pin header, 1 pin [form="♀ (female)"]
  ------------------------_2 = female pin header, 1 pin [form="♀ (female)"]
  +_-_2 = female pin header, 1 pin [form="♀ (female)"]
  V-AC_Out_2 = female pin header, 1 pin [form="♀ (female)"]
  LED_2 = LED - 3mm [color="Red (633nm)" package="3 mm [THT]"]
  47Ω_1/2W_2 = Resistor [tolerance=±5% resistance=47 package=THT]
  330Ω_5 = Resistor [tolerance=±5% resistance=4.7k package=THT]
  330Ω_6 = Resistor [tolerance=±5% resistance=1k package=THT]
  150Ω_3 = Resistor [tolerance=±5% resistance=150 package=THT]
  10kΩ_5 = Resistor [tolerance=±5% resistance=1k package=THT]
  2N3904_3 = NPN-Transistor [part_number=BC547 package="TO92 [THT]"]
  1N4001_4 = Rectifier Diode [part_number=1N4001 package="300 mil [THT]"]
  FUSE_3 = female pin header, 1 pin [form="♀ (female)"]
  ------------------------_3 = female pin header, 1 pin [form="♀ (female)"]
  +_-_3 = female pin header, 1 pin [form="♀ (female)"]
  V-AC_Out_3 = female pin header, 1 pin [form="♀ (female)"]
  LED_3 = LED - 3mm [color="Red (633nm)" package="3 mm [THT]"]
  2N2222A_2 = NPN-Transistor [package="TO92 [THT]"]
  100Ω_3 = Resistor [tolerance=±5% resistance=100 package=THT]
  100Ω_4 = Resistor [tolerance=±5% resistance=100 package=THT]
  10kΩ_6 = Resistor [tolerance=±5% resistance=10k package=THT]
  10kΩ_7 = Resistor [tolerance=±5% resistance=10k package=THT]
  100Ω_5 = Resistor [tolerance=±5% resistance=100 package=THT]
  V-IN = female pin header, 1 pin [form="♀ (female)"]
  V-OUT = female pin header, 1 pin [form="♀ (female)"]
  V-IN_2 = female pin header, 1 pin [form="♀ (female)"]
  V-OUT_2 = female pin header, 1 pin [form="♀ (female)"]
  V-IN_3 = female pin header, 1 pin [form="♀ (female)"]
  V-OUT_3 = female pin header, 1 pin [form="♀ (female)"]
  100nF/400V = female pin header, 1 pin [form="♀ (female)"]
  J15 = female pin header, 1 pin [form="♀ (female)"]
  J17 = female pin header, 1 pin [form="♀ (female)"]
  100nF/400V_2 = female pin header, 1 pin [form="♀ (female)"]
  J20 = female pin header, 1 pin [form="♀ (female)"]
  100nF/400V_3 = female pin header, 1 pin [form="♀ (female)"]
  47Ω_1/2W_3 = Resistor [tolerance=±5% resistance=47 package=THT]
  0_1uF_2 = Ceramic Capacitor [capacitance=100nF package="100 mil [THT, multilayer]"]
  100Ω_6 = Resistor [tolerance=±5% resistance=100 package=THT]
  ------------------------1 = female pin header, 2 pins [form="♀ (female)"]
  ------------------------2 = female pin header, 2 pins [form="♀ (female)"]
  ------------------------6 = female pin header, 2 pins [form="♀ (female)"]
  ------------------------5 = female pin header, 2 pins [form="♀ (female)"]
  ------------------------8 = female pin header, 2 pins [form="♀ (female)"]
  ------------------------7 = female pin header, 2 pins [form="♀ (female)"]
  ------------------------10 = female pin header, 2 pins [form="♀ (female)"]
  ------------------------9 = female pin header, 2 pins [form="♀ (female)"]
  ------------------------15 = female pin header, 2 pins [form="♀ (female)"]
  Water_Level_Tank = female pin header, 2 pins [form="♀ (female)"]
  ------------------------13 = female pin header, 2 pins [form="♀ (female)"]
  Field_Capacity = female pin header, 2 pins [form="♀ (female)"]
  ------------------------11 = female pin header, 2 pins [form="♀ (female)"]
  Soil_Moisture = female pin header, 2 pins [form="♀ (female)"]
  ------------------------17 = female pin header, 2 pins [form="♀ (female)"]
  ------------------------18 = female pin header, 2 pins [form="♀ (female)"]
  ------------------------19 = female pin header, 2 pins [form="♀ (female)"]
  10kΩ_8 = Resistor [tolerance=±5% resistance=10k package=THT]
  Arduino_Pro_Mini = Arduino Pro Mini v13
  ------------------------22 = female pin header, 2 pins [form="♀ (female)"]
  ------------------------23 = female pin header, 2 pins [form="♀ (female)"]
  ------------------------24 = female pin header, 2 pins [form="♀ (female)"]
  V_In_100-240_AC = female pin header, 2 pins [form="♀ (female)"]
  ------------------------26 = female pin header, 2 pins [form="♀ (female)"]
  ------------------------27 = female pin header, 2 pins [form="♀ (female)"]
  ------------------------28 = female pin header, 2 pins [form="♀ (female)"]
  Clock = male pin header, 4 pins [form="♂ (male)"]
  10kΩ_9 = Resistor [tolerance=±5% resistance=10k package=THT]
  Parte1 = OpenLog  # not connected
  LCD1 = male pin header, 4 pins [form="♂ (male)"]
  LCD2 = male pin header, 4 pins [form="♂ (male)"]
  LCD3 = male pin header, 2 pins [form="♂ (male)"]

nets:
  GND: LCD.pin1, V-.pin1, 1N4001_2.anode, 47uF.-, 47uF_2.-, 0_1uF.0, UA+5V.GND, 10kΩ.Pin_0, 10kΩ_2.Pin_1, 100Ω_2.Pin_0, 10kΩ_3.Pin_1, 2N3904.E, 10kΩ_4.Pin_1, 2N3904_2.E, 10kΩ_5.Pin_1, 2N3904_3.E, 100Ω_4.Pin_0, 10kΩ_6.Pin_1, 10kΩ_7.Pin_1, 0_1uF_2.0, ------------------------19.pin1, Arduino_Pro_Mini.GND, ------------------------26.pin1, Clock.pin4, LCD1.pin1, LCD2.pin1
  N1: LCD.pin2, 330Ω_2.Pin_0, 47uF_2.+, 0_1uF.1, UA+5V.output_voltage, SW_+.pin1, SW_M.pin1, SW_-.pin1, 150Ω.Pin_1, 330Ω_4.Pin_0, 150Ω_2.Pin_1, 330Ω_6.Pin_0, 150Ω_3.Pin_1, 100Ω_5.Pin_1, 100Ω_6.Pin_0, ------------------------15.pin1, ------------------------15.pin2, ------------------------17.pin1, ------------------------17.pin2, 10kΩ_8.Pin_0, ------------------------27.pin1, ------------------------27.pin2, Clock.pin3, 10kΩ_9.Pin_0, LCD1.pin2, LCD2.pin2
  N2: LCD.pin3, Arduino_Pro_Mini.D12/MISO
  N3: LCD.pin4, Arduino_Pro_Mini.D11_PWM/MOSI
  N4: 330Ω.Pin_0, 10kΩ_3.Pin_0, 2N3904.B
  N5: 330Ω.Pin_1, Arduino_Pro_Mini.D0/TX
  N6: 330Ω_2.Pin_1, LED.cathode
  N7: 1N4001.cathode, V-AC_Out_1.pin1, 150Ω.Pin_0
  N8: 1N4001.anode, +_-.pin1, LED.anode, 2N3904.C
  N9: V+.pin1, 1N4001_2.cathode, 47uF.+, UA+5V.input_voltage, 0_1uF_2.1, Arduino_Pro_Mini.RAW
  N10: Artesanos_Industriales_del_Sur.pin1, V-IN.pin1, V-IN_2.pin1, V-IN_3.pin1, J15.pin1, J17.pin1, J20.pin1, ------------------------9.pin1, ------------------------9.pin2
  N11: BY-SA_3_1.pin1, ------------------------1.pin1, ------------------------1.pin2, ------------------------6.pin1, ------------------------6.pin2, ------------------------8.pin1, ------------------------8.pin2, ------------------------10.pin1, ------------------------10.pin2
  N12: 10kΩ.Pin_1, Water_Level_Tank.pin1, Water_Level_Tank.pin2, Arduino_Pro_Mini.D13/SCK
  N13: 10kΩ_2.Pin_0, SW_-.pin2, Arduino_Pro_Mini.D7
  N14: 2N2222A.E, 100Ω_2.Pin_1, Arduino_Pro_Mini.A3
  N15: 2N2222A.B, ------------------------11.pin1, ------------------------11.pin2
  N16: 2N2222A.C, 100Ω_5.Pin_0
  N17: 100Ω.Pin_0, Arduino_Pro_Mini.D3_PWM
  N18: 100Ω.Pin_1, Soil_Moisture.pin1, Soil_Moisture.pin2
  N19: SW_+.pin2, 10kΩ_7.Pin_0, Arduino_Pro_Mini.D9_PWM
  N20: SW_M.pin2, 10kΩ_6.Pin_0, Arduino_Pro_Mini.D8
  N21: 47Ω_1/2W.Pin_0, 100nF/400V_3.pin1
  N22: 47Ω_1/2W.Pin_1, FUSE_1.pin1, V-OUT_2.pin1
  N23: ------------------------.pin1, ------------------------2.pin1, ------------------------2.pin2
  N24: 330Ω_3.Pin_0, 10kΩ_4.Pin_0, 2N3904_2.B
  N25: 330Ω_3.Pin_1, Arduino_Pro_Mini.D1/RX
  N26: 330Ω_4.Pin_1, LED_2.cathode
  N27: 150Ω_2.Pin_0, 1N4001_3.cathode, V-AC_Out_2.pin1
  N28: 2N3904_2.C, 1N4001_3.anode, +_-_2.pin1, LED_2.anode
  N29: FUSE_2.pin1, 47Ω_1/2W_2.Pin_1, V-OUT.pin1
  N30: ------------------------_2.pin1, ------------------------5.pin1, ------------------------5.pin2
  N31: 47Ω_1/2W_2.Pin_0, 100nF/400V_2.pin1
  N32: 330Ω_5.Pin_0, 10kΩ_5.Pin_0, 2N3904_3.B
  N33: 330Ω_5.Pin_1, Arduino_Pro_Mini.D2
  N34: 330Ω_6.Pin_1, LED_3.cathode
  N35: 150Ω_3.Pin_0, 1N4001_4.cathode, V-AC_Out_3.pin1
  N36: 2N3904_3.C, 1N4001_4.anode, +_-_3.pin1, LED_3.anode
  N37: FUSE_3.pin1, V-OUT_3.pin1, 47Ω_1/2W_3.Pin_1
  N38: ------------------------_3.pin1, ------------------------7.pin1, ------------------------7.pin2
  N39: 2N2222A_2.E, 100Ω_4.Pin_1, Arduino_Pro_Mini.A2
  N40: 2N2222A_2.B, ------------------------13.pin1, ------------------------13.pin2
  N41: 2N2222A_2.C, 100Ω_6.Pin_1
  N42: 100Ω_3.Pin_0, Arduino_Pro_Mini.D6_PWM
  N43: 100Ω_3.Pin_1, Field_Capacity.pin1, Field_Capacity.pin2
  N44: 100nF/400V.pin1, 47Ω_1/2W_3.Pin_0
  N45: ------------------------18.pin1, ------------------------18.pin2, 10kΩ_8.Pin_1, Arduino_Pro_Mini.A1
  N46: Arduino_Pro_Mini.A0, ------------------------28.pin1, 10kΩ_9.Pin_1
  N47: Arduino_Pro_Mini.D10_PWM/SS, LCD1.pin4
  N48: Arduino_Pro_Mini.D5_PWM, Clock.pin1
  N49: Arduino_Pro_Mini.D4, Clock.pin2
  N50: ------------------------22.pin1, ------------------------22.pin2, ------------------------23.pin1, ------------------------23.pin2, ------------------------24.pin1, ------------------------24.pin2, V_In_100-240_AC.pin1, V_In_100-240_AC.pin2
  N51: LCD2.pin3, LCD3.pin1
  N52: LCD2.pin4, LCD3.pin2

notes:
  D1 +  -
  Tx Rx + -
  UEC_AC_Mod. A-3S Rev.1.1
  Sensor-1
  SSR
  Sensor-2
  D3    +  -
  SCL SDA +  -
  - -
  -
  L  N  G
  Artesanos Industriales del Sur  aisur.org
  Power Supply 220VAC->9VDC
  Sensor-3
  SM-2
  D2 +  -
  D4 D5
  +  -
  SM-1
  Sensor-4
