# Fritzing sketch UEC_SAC_Comunication_Rev_1 (copia) (saved by Fritzing 0.9.0b)
circuit board: 5.00001cm x 5.00001cm
perfboards: 1

parts:
  LCD3 = male pin header, 3 pins [form="♂ (male)"]
  J19 = female pin header, 2 pins [form="♀ (female)"]
  SparkCore = Spark Core (v1.0)
  A25L032 = 23LCV1024 [part_number=23LCV1024 package="DIP (Dual Inline) [THT]"]
  LCD5 = male pin header, 12 pins [form="♂ (male)"]
  CD74HC4052 = IC, DIP package, 16 pins [chip_label=IC]
  LCD4 = male pin header, 8 pins [form="♂ (male)"]
  LCD7 = male pin header, 7 pins [form="♂ (male)"]
  MCP1700-4002E = NPN-Transistor [package="TO92 [THT]"]
  C1 = Ceramic Capacitor [capacitance=1µF package="100 mil [THT, multilayer]"]
  C2 = Ceramic Capacitor [capacitance=1µF package="100 mil [THT, multilayer]"]
  J20 = female pin header, 2 pins [form="♀ (female)"]

nets:
  GND: LCD3.pin1, SparkCore.GND, A25L032.VSS, LCD5.pin2, LCD5.pin7, CD74HC4052.pin6, CD74HC4052.pin8, LCD4.pin6, LCD7.pin1, MCP1700-4002E.E, C1.1, C2.1, J20.pin1
  N1: LCD3.pin3, SparkCore.VIN, LCD4.pin7, LCD7.pin2, MCP1700-4002E.C, C1.0
  N2: J19.pin1, SparkCore.TX
  N3: J19.pin2, SparkCore.RX
  N4: SparkCore.A0, LCD7.pin3
  N5: SparkCore.A1, LCD4.pin8
  N6: SparkCore.A2, A25L032.CS_
  N7: SparkCore.A3, A25L032.SCK
  N8: SparkCore.A4, A25L032.SO/SIO1
  N9: SparkCore.A5, A25L032.SI/SIO0
  N10: SparkCore.A6, LCD5.pin11
  N11: SparkCore.A7, LCD5.pin6
  N12: SparkCore.D0, CD74HC4052.pin3
  N13: SparkCore.D1, CD74HC4052.pin13
  N14: SparkCore.D2, LCD5.pin5
  N15: SparkCore.D3, LCD7.pin7
  N16: SparkCore.D4, LCD4.pin1
  N17: SparkCore.D5, LCD5.pin12
  N18: SparkCore.D6, CD74HC4052.pin10
  N19: SparkCore.D7, CD74HC4052.pin9
  N20: SparkCore.3V3*, A25L032.VCC, CD74HC4052.pin16, J20.pin2
  N21: LCD5.pin1, MCP1700-4002E.B, C2.0
  N22: LCD5.pin9, CD74HC4052.pin14
  N23: LCD5.pin10, CD74HC4052.pin5
  N24: CD74HC4052.pin1, LCD7.pin4
  N25: CD74HC4052.pin2, LCD4.pin5
  N26: CD74HC4052.pin12, LCD7.pin5
  N27: CD74HC4052.pin15, LCD4.pin4

notes:
  UEC_CS_Rev.1
  D1 +  -
  D3    +  -
  TXO
  +5V
  +
  sacultivo.com
  Artesanos Industriales del Sur www.aisur.org
  GND
  RXI
  GPS
  GSM
  RXM
  RX
  EN
  RX0
  RX2
  TX0
  RX1
  TX1
  S0
  TXM
  PPS
  VIN
  TX
  S1
  TX2
  RX3
  TX3
  VCC
  VIO
  KEY
  RST
  PS
  +3.3V
  RF
  CC By-Sa 4.0
  MEMORY
