# Fritzing sketch modulo_riego (saved by Fritzing 0.7.4b)

parts:
  Arduino1 = Arduino
  Relay = Relay [part_number=FRS1B-S package=THT]
  Vin_12V = female pin header, 2 pins [form="♀ (female)"]
  Pump = female pin header, 2 pins [form="♀ (female)"]
  LED = RGB LED - (4 legs) [package="5 mm [THT]"]
  Sonda_S1 = female pin header, 2 pins [form="♀ (female)"]
  Sonda_S2 = female pin header, 2 pins [form="♀ (female)"]
  R1 = Resistor [tolerance=±5% resistance=1k package=THT]
  R2 = Resistor [tolerance=±5% resistance=1k package=THT]
  R3 = Resistor [tolerance=±5% resistance=1k package=THT]
  R5 = Resistor [tolerance=±5% resistance=10k package=THT]
  R4 = Resistor [tolerance=±5% resistance=10k package=THT]

nets:
  N1: Arduino1.GND, Relay.COIL1, Vin_12V.pin2, Pump.pin1, LED.common_anode, R5.Pin_0, R4.Pin_0
  N2: Arduino1.D7, Relay.COIL2
  N3: Arduino1.D6, R1.Pin_1
  N4: Arduino1.D5, R2.Pin_1
  N5: Arduino1.D4, R3.Pin_1
  N6: Arduino1.D3, Sonda_S2.pin2, R5.Pin_1
  N7: Arduino1.D2, Sonda_S1.pin2, R4.Pin_1
  N8: Arduino1.+5V, Sonda_S1.pin1, Sonda_S2.pin1
  N9: Arduino1.VIN, Relay.C1, Relay.C2, Vin_12V.pin1
  N10: Relay.B, Pump.pin2
  N11: LED.red_cathode, R3.Pin_0
  N12: LED.green_cathode, R2.Pin_0
  N13: LED.blue_cathode, R1.Pin_0
