# Fritzing sketch modulo_riegoRev02 (saved by Fritzing 0.7.4b)

parts:
  K3 = Relay [part_number=FRS1B-S package=THT]
  R11 = Resistor [tolerance=±5% resistance=1k package=THT]  # not connected
  R12 = Resistor [tolerance=±5% resistance=1k package=THT]  # not connected
  R13 = Resistor [tolerance=±5% resistance=1k package=THT]  # not connected
  LED_(RGB)1 = RGB LED - (4 legs) [package="5 mm [THT]"]  # not connected
  Vin_12V = female pin header, 2 pins [form="♀ (female)"]  # not connected
  Bomba = female pin header, 2 pins [form="♀ (female)"]  # not connected
  R14 = Resistor [tolerance=±5% resistance=10k package=THT]  # not connected
  R15 = Resistor [tolerance=±5% resistance=10k package=THT]  # not connected
  Sonda_II = female pin header, 2 pins [form="♀ (female)"]  # not connected
  Sonda_I = female pin header, 2 pins [form="♀ (female)"]  # not connected
  Parte5 = Arduino Wireless SD Shield [part_number=rev05]  # not connected

nets:
  N1: K3.C1, K3.C2

custom parts:
  Arduino Wireless SD Shield: The Wireless SD shield allows an Arduino board to communicate wirelessly using a wireless module. It is based on the Xbee modules from Digi, but can use any module with the same footprint. The module can communicate up to 100 feet indoors or 300 feet outdoors (with line-of-sight). It can be used as a serial/usb replacement or you can put it into a command mode and configure it for a variety of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
