# Fritzing sketch modulo_riego_PCB (saved by Fritzing 0.7.4b)

parts:
  Parte1 = Arduino Wireless SD Shield
  K1 = Relay [part_number=FRS1B-S package=THT]
  R1 = Resistor [tolerance=±5% resistance=1k package=THT]
  R2 = Resistor [tolerance=±5% resistance=1k package=THT]
  R3 = Resistor [tolerance=±5% resistance=1k package=THT]
  R4 = Resistor [tolerance=±5% resistance=10k package=THT]
  R5 = Resistor [tolerance=±5% resistance=10k package=THT]
  J1 = female pin header, 2 pins [form="♀ (female)"]
  J2 = female pin header, 2 pins [form="♀ (female)"]
  Pumb = female pin header, 2 pins [form="♀ (female)"]
  V_12V = female pin header, 2 pins [form="♀ (female)"]
  LED1 = RGB LED (com. anode, rbg) [package="5 mm [THT]"]

nets:
  N1: Parte1.+5V, Parte1.N$79, Parte1.N$99, J1.pin1, J2.pin1
  N2: Parte1.GND, Parte1.N$75, Parte1.N$109, Parte1.N$111, Parte1.N$116, Parte1.N$129, K1.COIL1, R4.Pin_0, R5.Pin_0, Pumb.pin2, V_12V.pin2, LED1.common_anode
  N3: Parte1.SD_CS, Parte1.N$77, R3.Pin_1
  N4: Parte1.D6, Parte1.N$122, R1.Pin_1
  N5: Parte1.D2, Parte1.N$64, Parte1.N$89, R4.Pin_1, J2.pin2
  N6: Parte1.D3, Parte1.N$60, Parte1.N$76, R5.Pin_1, J1.pin2
  N7: Parte1.D5, Parte1.N$32, R2.Pin_1
  N8: Parte1.D7, Parte1.N$141, K1.COIL2
  N9: Parte1.VIN, Parte1.N$112, Parte1.N$139, Parte1.N$181, K1.C1, K1.C2, V_12V.pin1
  N10: Parte1.N$55, Parte1.N$160, R2.Pin_0, LED1.blue_cathode
  N11: Parte1.N$70, R1.Pin_0, LED1.red_cathode
  N12: Parte1.N$72, K1.A
  N13: Parte1.N$117, Parte1.N$165, R3.Pin_0, LED1.green_cathode
  N14: Parte1.N$119, Parte1.N$131, K1.B, Pumb.pin1
